# Fritzing sketch biribiri (saved by Fritzing 0.9.4)
breadboards: 1

parts:
  R1 = Resistor [tolerance=±5% resistance=3.3k package=THT]
  R2 = Resistor [tolerance=±5% resistance=22k package=THT]
  R3 = Resistor [tolerance=±5% resistance=3.3k package=THT]
  R4 = Resistor [tolerance=±5% resistance=10k package=THT]
  D1 = Rectifier Diode [part_number=1N4001 package="300 mil [THT]"]
  D2 = Rectifier Diode [part_number=1N4001 package="300 mil [THT]"]
  パーツ1 = Arduino Uno (Rev3)
  R5 = Resistor [tolerance=±5% resistance=10k package=THT]
  2SC1815GR = NPN-Transistor [package="TO92 [THT]"]
  D1(Orange)3 = Rectifier Diode [part_number=D1 package="300 mil [THT]"]
  2SC1815GR_2 = NPN-Transistor [package="TO92 [THT]"]
  Solenoid_valve = Solenoid

nets:
  N1: R1.Pin_0, R5.Pin_1
  water surface2: R1.Pin_1
  N2: R2.Pin_0, R4.Pin_0, パーツ1.5V, R5.Pin_0
  N3: R2.Pin_1, D2.cathode, 2SC1815GR.C
  N4: R3.Pin_0, D1.anode
  water surface1: R3.Pin_1
  N5: R4.Pin_1, D2.anode, パーツ1.D2
  N6: D1.cathode, 2SC1815GR.B
  N7: パーツ1.D13/SCK, 2SC1815GR_2.B
  GND: パーツ1.GND, 2SC1815GR.E
  Power 12V: D1(Orange)3.cathode, 2SC1815GR_2.C, Solenoid_valve.pin2
  N8: D1(Orange)3.anode, 2SC1815GR_2.E, Solenoid_valve.pin1
