# Fritzing sketch potarhythm (saved by Fritzing 0.9.4)
breadboards: 1

parts:
  パーツ1 = Arduino Ethernet Shield (Rev3)
  D1(Orange) = Rectifier Diode [part_number=D0 package="300 mil [THT]"]
  2SC1815GR = NPN-Transistor [package="TO92 [THT]"]
  Solenoid_valve1 = Solenoid
  J1 = Power Jack [package=power_jack_slot]
  D1(Orange)1 = Rectifier Diode [part_number=D1 package="300 mil [THT]"]
  2SC1815GR_2 = NPN-Transistor [package="TO92 [THT]"]
  Solenoid_valve2 = Solenoid
  D1(Orange)2 = Rectifier Diode [part_number=D2 package="300 mil [THT]"]
  2SC1815GR_3 = NPN-Transistor [package="TO92 [THT]"]
  Solenoid_valve3 = Solenoid
  D1(Orange)3 = Rectifier Diode [part_number=D3 package="300 mil [THT]"]
  2SC1815GR_4 = NPN-Transistor [package="TO92 [THT]"]
  Solenoid_valve4 = Solenoid
  TLP(P521) = TLP621 [package=THT]
  DIN1 = DIN-5 jack (MIDI) [package=THT]
  R1 = Resistor [tolerance=±5% resistance=220 package=THT]
  R2 = Resistor [tolerance=±5% resistance=1k package=THT]

nets (from the schematic view):
  N1: パーツ1.5V, R2.Pin_1
  N2: パーツ1.D8, 2SC1815GR_2.C
  N3: パーツ1.PWM_D9, 2SC1815GR_3.C
  N4: パーツ1.ETH_CS, 2SC1815GR_4.C
  GND: パーツ1.GND, 2SC1815GR.B, J1.GND, 2SC1815GR_2.B, 2SC1815GR_3.B, 2SC1815GR_4.B, TLP(P521).Pin_3, DIN1.2, DIN1.GND
  N5: パーツ1.RX/D0, TLP(P521).Pin_4, R2.Pin_0
  N6: パーツ1.D7, 2SC1815GR.C
  power(12V): D1(Orange).cathode, Solenoid_valve1.pin2, J1.PWR, D1(Orange)1.cathode, Solenoid_valve2.pin2, D1(Orange)2.cathode, Solenoid_valve3.pin2, D1(Orange)3.cathode, Solenoid_valve4.pin2
  N7: D1(Orange).anode, 2SC1815GR.E, Solenoid_valve1.pin1
  N8: D1(Orange)1.anode, 2SC1815GR_2.E, Solenoid_valve2.pin1
  N9: D1(Orange)2.anode, 2SC1815GR_3.E, Solenoid_valve3.pin1
  N10: D1(Orange)3.anode, 2SC1815GR_4.E, Solenoid_valve4.pin1
  N11: TLP(P521).Pin_1, R1.Pin_0
  N12: TLP(P521).Pin_2, DIN1.5
  N13: DIN1.4, R1.Pin_1
