# Fritzing sketch ptr_2 (saved by Fritzing 0.9.4)
breadboards: 2

parts:
  D1(Orange) = Rectifier Diode [part_number=D0 package="300 mil [THT]"]
  2SC1815GR = NPN-Transistor [package="TO92 [THT]"]
  Solenoid_valve1 = Solenoid
  J1 = Power Jack [package=power_jack_slot]
  D1(Orange)1 = Rectifier Diode [part_number=D1 package="300 mil [THT]"]
  2SC1815GR_2 = NPN-Transistor [package="TO92 [THT]"]
  Solenoid_valve2 = Solenoid
  TLP621 = TLP621 [package=THT]
  DIN1 = DIN-5 jack (MIDI) [package=THT]
  R1 = Resistor [tolerance=±5% resistance=220 package=THT]
  R2 = Resistor [tolerance=±5% resistance=1k package=THT]
  デュアル・モータードライバTB6612FNG = Motor Driver 1A Dual TB6612FNG
  MotorFader1 = DC Motor
  MotorFader2 = DC Motor
  Motor_fader_R1 = Slide Potentiometer [maximum_resistance=100kΩ]
  Motor_fader_R2 = Slide Potentiometer [maximum_resistance=100kΩ]
  Solenoid_valve3 = Solenoid
  D1(Orange)2 = Rectifier Diode [part_number=D1 package="300 mil [THT]"]
  2SC1815GR_3 = NPN-Transistor [package="TO92 [THT]"]
  R6 = Resistor [tolerance=±5% resistance=3.3k package=THT]
  R7 = Resistor [tolerance=±5% resistance=3.3k package=THT]
  R8 = Resistor [tolerance=±5% resistance=22k package=THT]
  R9 = Resistor [tolerance=±5% resistance=10k package=THT]
  R10 = Resistor [tolerance=±5% resistance=10k package=THT]
  D3 = Rectifier Diode [part_number=1N4001 package="300 mil [THT]"]
  D4 = Rectifier Diode [part_number=1N4001 package="300 mil [THT]"]
  2SC1815GR_4 = NPN-Transistor [package="TO92 [THT]"]
  Arduino_UNO = Arduino Uno (Rev3)

nets (from the schematic view):
  power(12V): D1(Orange).cathode, Solenoid_valve1.pin2, J1.PWR, D1(Orange)1.cathode, Solenoid_valve2.pin2, デュアル・モータードライバTB6612FNG.VM, Solenoid_valve3.pin2, D1(Orange)2.cathode
  N1: D1(Orange).anode, 2SC1815GR.E, Solenoid_valve1.pin1
  GND: 2SC1815GR.B, J1.GND, 2SC1815GR_2.B, TLP621.Pin_3, DIN1.2, DIN1.GND, デュアル・モータードライバTB6612FNG.GND, Motor_fader_R1.leg2, Motor_fader_R2.leg2, 2SC1815GR_3.B, 2SC1815GR_4.E, Arduino_UNO.GND
  N2: 2SC1815GR.C, Arduino_UNO.D11_PWM/MOSI
  N3: D1(Orange)1.anode, 2SC1815GR_2.E, Solenoid_valve2.pin1
  N4: 2SC1815GR_2.C, Arduino_UNO.D12/MISO
  N5: TLP621.Pin_1, R1.Pin_0
  N6: TLP621.Pin_2, DIN1.5
  N7: TLP621.Pin_4, R2.Pin_0, Arduino_UNO.D0/RX
  N8: DIN1.4, R1.Pin_1
  5v: R2.Pin_1, デュアル・モータードライバTB6612FNG.VCC, Motor_fader_R1.leg1, Motor_fader_R2.leg1, R8.Pin_0, R9.Pin_0, R10.Pin_0, Arduino_UNO.5V
  N9: デュアル・モータードライバTB6612FNG.B01, MotorFader2.pin_1
  N10: デュアル・モータードライバTB6612FNG.B02, MotorFader2.pin_2
  N11: デュアル・モータードライバTB6612FNG.A02, MotorFader1.pin_2
  N12: デュアル・モータードライバTB6612FNG.A01, MotorFader1.pin_1
  N13: デュアル・モータードライバTB6612FNG.PWMA, Arduino_UNO.D5_PWM
  N14: デュアル・モータードライバTB6612FNG.AIN2, Arduino_UNO.D4
  N15: デュアル・モータードライバTB6612FNG.AIN1, Arduino_UNO.D3_PWM
  N16: デュアル・モータードライバTB6612FNG.STBY, Arduino_UNO.D9_PWM
  N17: デュアル・モータードライバTB6612FNG.BIN1, Arduino_UNO.D7
  N18: デュアル・モータードライバTB6612FNG.BIN2, Arduino_UNO.D8
  N19: デュアル・モータードライバTB6612FNG.PWMB, Arduino_UNO.D6_PWM
  N20: Motor_fader_R1.wiper, Arduino_UNO.A0
  N21: Motor_fader_R2.wiper, Arduino_UNO.A1
  N22: Solenoid_valve3.pin1, D1(Orange)2.anode, 2SC1815GR_3.E
  N23: 2SC1815GR_3.C, Arduino_UNO.D13/SCK
  N24: R6.Pin_0, D3.anode
  Water surface1: R6.Pin_1
  N25: R7.Pin_0, R9.Pin_1
  water surface2: R7.Pin_1
  N26: R8.Pin_1, D4.cathode, 2SC1815GR_4.C
  N27: R10.Pin_1, D4.anode, Arduino_UNO.D2
  N28: D3.cathode, 2SC1815GR_4.B
