# Fritzing sketch ptr_2_mortor (saved by Fritzing 0.9.4)
breadboards: 2

parts:
  デュアル・モータードライバTB6612FNG = Motor Driver 1A Dual TB6612FNG
  MotorFader1 = DC Motor
  MotorFader2 = DC Motor
  Motor_fader_R1 = Slide Potentiometer [maximum_resistance=100kΩ]
  Motor_fader_R2 = Slide Potentiometer [maximum_resistance=100kΩ]
  パーツ1 = Arduino Uno (Rev3)

nets:
  GND: デュアル・モータードライバTB6612FNG.GND, Motor_fader_R1.leg2, Motor_fader_R2.leg2, パーツ1.GND
  N1: デュアル・モータードライバTB6612FNG.B01, MotorFader2.pin_1
  N2: デュアル・モータードライバTB6612FNG.B02, MotorFader2.pin_2
  N3: デュアル・モータードライバTB6612FNG.A02, MotorFader1.pin_2
  N4: デュアル・モータードライバTB6612FNG.A01, MotorFader1.pin_1
  5v: デュアル・モータードライバTB6612FNG.VCC, Motor_fader_R1.leg1, Motor_fader_R2.leg1, パーツ1.5V
  power(12V): デュアル・モータードライバTB6612FNG.VM
  N5: デュアル・モータードライバTB6612FNG.PWMA, パーツ1.D5_PWM
  N6: デュアル・モータードライバTB6612FNG.AIN2, パーツ1.D4
  N7: デュアル・モータードライバTB6612FNG.AIN1, パーツ1.D3_PWM
  N8: デュアル・モータードライバTB6612FNG.STBY, パーツ1.D9_PWM
  N9: デュアル・モータードライバTB6612FNG.BIN1, パーツ1.D7
  N10: デュアル・モータードライバTB6612FNG.BIN2, パーツ1.D8
  N11: デュアル・モータードライバTB6612FNG.PWMB, パーツ1.D6_PWM
  N12: Motor_fader_R1.wiper, パーツ1.A0
  N13: Motor_fader_R2.wiper, パーツ1.A1
